# Fritzing sketch rampart_pico (saved by Fritzing 1.0.6)
circuit board: 8.80001cm x 6.50001cm
breadboards: 2

parts:
  10k = Rotary Potentiometer (Small) [maximum_resistance=100kΩ knob_status=50% power=0.5W package=THT]
  10k_2 = Rotary Potentiometer (Small) [maximum_resistance=100kΩ knob_status=50% power=0.5W package=THT]
  10k_3 = Rotary Potentiometer (Small) [maximum_resistance=100kΩ knob_status=50% power=0.5W package=THT]
  -/+ = female pin header, 2 pins [form="♀ (female)"]
  104 = Capacitor [package=cap-pth-5mm]
  105 = Capacitor [package=cap-pth-5mm]
  10K2 = Rotary Potentiometer (Small) [maximum_resistance=10kΩ knob_status=50% power=0.5W package=THT]
  SSD1306 = OLED Mono 0.56 inch blue or white
  CV1 = female pin header, 3 pins [form="♀ (female)"]
  CV2 = female pin header, 3 pins [form="♀ (female)"]
  RE1 = Rotary Encoder [package=THT]
  1uF = Electrolytic Capacitor [capacitance=1µF voltage=35V package="100 mil [THT, electrolytic]"]
  pico2zero = Waveshare rp2040-zero tht [package=THT]
  a/clk< = 3.5mm Audio Jack-wq-pj320b.fzpz [package=audio-jack-3.5mm-smd]
  ADS1115 = female pin header, 10 pins [form="♀ (female)"]
  v+ = female pin header, 3 pins [form="♀ (female)"]
  v- = female pin header, 3 pins [form="♀ (female)"]
  2N3904 = NPN-Transistor [package="TO92 [THT]"]
  J8/9 = female pin header, 2 pins [form="♀ (female)"]
  BUS = female pin header, 7 pins [form="♀ (female)"]
  midi> = 3.5mm Audio Jack-wq-pj320b.fzpz [package=audio-jack-3.5mm-smd]
  audio> = 3.5mm Audio Jack-wq-pj320b.fzpz [package=audio-jack-3.5mm-smd]
  S7 = SPST Switch [package=switch-spdt_kit]
  104_2 = Capacitor [package=cap-pth-5mm]
  TXRX = female pin header, 3 pins [form="♀ (female)"]
  220 = Resistor [tolerance=±1% power=0.25W resistance=220 package=THT]
  220_2 = Resistor [tolerance=±1% power=0.25W resistance=220 package=THT]
  10K = Resistor [tolerance=±1% power=0.25W resistance=10k package=THT]
  10k_4 = Resistor [tolerance=±1% power=0.25W resistance=10k package=THT]
  100Ω = Resistor [tolerance=±1% power=0.25 resistance=100 package=THT]
  10K_2 = Resistor [tolerance=±1% power=0.25 resistance=10k package=THT]
  100Ω_2 = Resistor [tolerance=±1% power=0.25 resistance=100 package=THT]
  1k = Resistor [tolerance=±1% power=0.25W resistance=1k package=THT]
  1k_2 = Resistor [tolerance=±1% power=0.25W resistance=1k package=THT]
  1k_3 = Resistor [tolerance=±1% power=0.25W resistance=1k package=THT]

nets (from the schematic view):
  GND: 10k.leg1, 10k_2.leg1, 10k_3.leg1, -/+.pin1, 104.2, SSD1306.GND, RE1.GND, RE1.SW-2, 1uF.-, pico2zero.Pin_2, a/clk<.pin_4, ADS1115.pin2, v-.pin1, v-.pin2, v-.pin3, 2N3904.E, BUS.pin2, midi>.pin_4, audio>.pin_4, 104_2.2, 10K_2.Pin_1, 1k.Pin_1, 1k_2.Pin_1, 1k_3.Pin_1
  N1: 10k.wiper, pico2zero.Pin_4
  V++: 10k.leg2, 10k_2.leg2, 10k_3.leg2, SSD1306.VCC, pico2zero.Pin_3, ADS1115.pin1, v+.pin1, v+.pin2, v+.pin3, J8/9.pin2, BUS.pin1, S7.O, 104_2.1, 220_2.Pin_0, 10k_4.Pin_1
  N2: 10k_2.wiper, pico2zero.Pin_5
  N3: 10k_3.wiper, pico2zero.Pin_6
  N4: -/+.pin2, 10K2.leg1, 1uF.+
  N5: 104.1, 10K2.leg2, 100Ω_2.Pin_1
  AOUT: 105.1, pico2zero.Pin_12
  N6: 105.2, ADS1115.pin10, S7.S, 100Ω.Pin_1, 10K_2.Pin_0
  N7: 10K2.wiper, 100Ω.Pin_0
  SDA1: SSD1306.SDA, pico2zero.Pin_21, BUS.pin5
  SCL1: SSD1306.SCL, pico2zero.Pin_20, BUS.pin4
  N8: CV1.pin1, ADS1115.pin7
  N9: CV1.pin2, ADS1115.pin8
  N10: CV1.pin3, ADS1115.pin9
  N11: CV2.pin1, 1k.Pin_0
  N12: CV2.pin2, 1k_2.Pin_0
  N13: CV2.pin3, 1k_3.Pin_0
  ENCA: RE1.Pin-A, pico2zero.Pin_14
  ENCB: RE1.Pin-B, pico2zero.Pin_13
  ENCBUT: RE1.SW-1, pico2zero.Pin_15
  N14: pico2zero.Pin_7, J8/9.pin1
  SCL0: pico2zero.Pin_10, ADS1115.pin3
  SDA0: pico2zero.Pin_11, ADS1115.pin4
  xsht: pico2zero.Pin_16, BUS.pin3
  BUT2: pico2zero.Pin_17, BUS.pin6
  BUT1: pico2zero.Pin_18, BUS.pin7
  N15: pico2zero.Pin_19, TXRX.pin3
  N16: pico2zero.Pin_22, 2N3904.C, TXRX.pin2, 10k_4.Pin_0
  N17: pico2zero.Pin_23, TXRX.pin1, 220.Pin_1
  N18: a/clk<.pin_2, 10K.Pin_0
  AIN: a/clk<.Pin_3, S7.P
  N19: 2N3904.B, 10K.Pin_1
  N20: midi>.pin_2, 220.Pin_0
  N21: midi>.Pin_3, 220_2.Pin_1
  N22: audio>.pin_2, audio>.Pin_3, 100Ω_2.Pin_0

notes:
  rampart II
  blueprint@poetaster.de 2026

custom parts:
  OLED Mono 0.56 inch blue or white: OLED, I2C 3.3V - 5V Blue and White text versions
  Rotary Encoder: Rotary Encoder with push button
  Waveshare rp2040-zero tht: .RP2040-Zero, A Low-Cost, High-Performance Pico-Like MCU Board Based On Raspberry Pi Microcontroller RP2040. This varant is THT without the extra connections.
  3.5mm Audio Jack-wq-pj320b.fzpz: 3.5mm Audio Jack WQP-PJ320B is a SMD jack, dia 1/8 inch, female, right angle and through hole.
